// Logisim project ALU.circ as structural Verilog: 13 circuits, main circuit ALU
module ALU (
  input  s2,
  input  s1,
  input  s0,
  input  [15:0] a,
  input  [15:0] b,
  output [15:0] r,
  output Overflow,
  output Division_by_zero
);

  Selection selection_1 (
    .in_3(s2), .in_4(s1), .in_5(s0), .out_52(Overflow), .out_53(Division_by_zero));  // open: in_1, in_2, in_6, in_7, in_8, in_9, in_10, in_11, in_12, in_13, in_14, in_15, in_16, in_17, in_18, in_19, in_20, in_21, in_22, in_23, in_24, in_25, in_26, in_27, in_28, in_29, in_30, in_31, in_32, in_33, in_34, in_35, out_36, out_37, out_38, out_39, out_40, out_41, out_42, out_43, out_44, out_45, out_46, out_47, out_48, out_49, out_50, out_51
endmodule

// ALU
module Selection (
  input  in_1,
  input  in_2,
  input  in_3,
  input  in_4,
  input  in_5,
  input  in_6,
  input  in_7,
  input  in_8,
  input  in_9,
  input  in_10,
  input  in_11,
  input  in_12,
  input  in_13,
  input  in_14,
  input  in_15,
  input  in_16,
  input  in_17,
  input  in_18,
  input  in_19,
  input  in_20,
  input  in_21,
  input  in_22,
  input  in_23,
  input  in_24,
  input  in_25,
  input  in_26,
  input  in_27,
  input  in_28,
  input  in_29,
  input  in_30,
  input  in_31,
  input  in_32,
  input  in_33,
  input  in_34,
  input  in_35,
  output out_36,
  output out_37,
  output out_38,
  output out_39,
  output out_40,
  output out_41,
  output out_42,
  output out_43,
  output out_44,
  output out_45,
  output out_46,
  output out_47,
  output out_48,
  output out_49,
  output out_50,
  output out_51,
  output out_52,
  output out_53
);

  wire n16bit_adder_1_overflow, n16bit_divider_1_overflow, n16bit_multiplier_1_overflow,
       n16bit_subtractor_1_overflow, nor_1_out;
  wire [15:0] n16bit_adder_1_out_3, n16bit_divider_1_out_4, n16bit_divider_2_out_4,
       n16bit_multiplier_1_out_3, n16bit_subtractor_1_out_3;

  _16bit_Adder u_16bit_adder_1 (
    .in_1({in_19, in_18, in_17, in_16, in_15, in_14, in_13, in_12, in_11, in_10, in_9, in_8, in_7, in_6, in_2, in_1}),
    .in_2({in_35, in_34, in_33, in_32, in_31, in_30, in_29, in_28, in_27, in_26, in_25, in_24, in_23, in_22, in_21, in_20}),
    .out_3(n16bit_adder_1_out_3), .Overflow(n16bit_adder_1_overflow));  // open: Carry_Out
  _16bit_Subtractor u_16bit_subtractor_1 (
    .in_1({in_19, in_18, in_17, in_16, in_15, in_14, in_13, in_12, in_11, in_10, in_9, in_8, in_7, in_6, in_2, in_1}),
    .in_2({in_35, in_34, in_33, in_32, in_31, in_30, in_29, in_28, in_27, in_26, in_25, in_24, in_23, in_22, in_21, in_20}),
    .out_3(n16bit_subtractor_1_out_3), .Overflow(n16bit_subtractor_1_overflow));
  _16bit_Multiplier u_16bit_multiplier_1 (
    .in_1({in_19, in_18, in_17, in_16, in_15, in_14, in_13, in_12, in_11, in_10, in_9, in_8, in_7, in_6, in_2, in_1}),
    .in_2({in_35, in_34, in_33, in_32, in_31, in_30, in_29, in_28, in_27, in_26, in_25, in_24, in_23, in_22, in_21, in_20}),
    .out_3(n16bit_multiplier_1_out_3), .Overflow(n16bit_multiplier_1_overflow));
  _16bit_Divider u_16bit_divider_1 (
    .in_1({in_19, in_18, in_17, in_16, in_15, in_14, in_13, in_12, in_11, in_10, in_9, in_8, in_7, in_6, in_2, in_1}),
    .in_2({in_35, in_34, in_33, in_32, in_31, in_30, in_29, in_28, in_27, in_26, in_25, in_24, in_23, in_22, in_21, in_20}),
    .Option(1'b0), .out_4(n16bit_divider_1_out_4), .Overflow(n16bit_divider_1_overflow));
  _16bit_Divider u_16bit_divider_2 (
    .in_1({in_19, in_18, in_17, in_16, in_15, in_14, in_13, in_12, in_11, in_10, in_9, in_8, in_7, in_6, in_2, in_1}),
    .in_2({in_35, in_34, in_33, in_32, in_31, in_30, in_29, in_28, in_27, in_26, in_25, in_24, in_23, in_22, in_21, in_20}),
    .Option(1'b1), .out_4(n16bit_divider_2_out_4));  // open: Overflow
  Multiplexer #(.select(3), .width(16), .enable("false")) multiplexer_1 (
    .in0(n16bit_adder_1_out_3), .in1(n16bit_subtractor_1_out_3), .in2(n16bit_multiplier_1_out_3),
    .in3(n16bit_divider_1_out_4), .in4(n16bit_divider_2_out_4),
    .out({out_52, out_50, out_49, out_48, out_47, out_46, out_45, out_44, out_43, out_42, out_41, out_40, out_39, out_38, out_37, out_36}),
    .sel({in_3, in_4, in_5}));  // open: in5, in6, in7
  Multiplexer #(.select(3), .enable("false")) multiplexer_2 (
    .in0(n16bit_adder_1_overflow), .in1(n16bit_subtractor_1_overflow), .in2(n16bit_multiplier_1_overflow),
    .in3(n16bit_divider_1_overflow), .in4(1'b0), .out(out_51), .sel({in_3, in_4, in_5}));  // open: in5, in6, in7
  Multiplexer #(.select(3), .enable("false")) multiplexer_3 (
    .in0(1'b0), .in1(1'b0), .in2(1'b0), .in3(nor_1_out), .in4(nor_1_out), .out(out_53),
    .sel({in_3, in_4, in_5}));  // open: in5, in6, in7
  nor nor_1 (nor_1_out, in_20, in_21, in_22, in_23, in_24, in_25, in_26, in_27, in_28, in_29, in_30, in_31, in_32, in_33, in_34, in_35);
endmodule

// HA
module Half_Adder (
  input  in_1,
  input  in_2,
  output Sum,
  output Carry
);

  wire not_1_out, or_1_out;

  or or_1 (or_1_out, in_1, in_2);
  and and_1 (Carry, in_1, in_2);
  not not_1 (not_1_out, Carry);
  and and_2 (Sum, or_1_out, not_1_out);
endmodule

// FA
module Full_Adder (
  input  in_1,
  input  in_2,
  input  Carry_In,
  output Sum,
  output Carry_Out
);

  wire half_adder_1_carry, half_adder_1_sum, half_adder_2_carry;

  Half_Adder half_adder_1 (.in_1(in_1), .in_2(in_2), .Sum(half_adder_1_sum), .Carry(half_adder_1_carry));
  Half_Adder half_adder_2 (.in_1(half_adder_1_sum), .in_2(Carry_In), .Sum(Sum), .Carry(half_adder_2_carry));
  or or_1 (Carry_Out, half_adder_1_carry, half_adder_2_carry);
endmodule

// Add
module _16bit_Adder (
  input  [15:0] in_1,
  input  [15:0] in_2,
  output [15:0] out_3,
  output Carry_Out,
  output Overflow
);

  wire and_1_out, and_2_out, full_adder_1_carry_out, full_adder_2_carry_out, full_adder_3_carry_out,
       full_adder_4_carry_out, full_adder_5_carry_out, full_adder_6_carry_out, full_adder_7_carry_out,
       full_adder_8_carry_out, full_adder_9_carry_out, full_adder_10_carry_out, full_adder_11_carry_out,
       full_adder_12_carry_out, full_adder_13_carry_out, full_adder_14_carry_out, full_adder_15_carry_out,
       not_1_out, not_2_out, not_3_out;

  Full_Adder full_adder_1 (
    .in_1(1'b0), .in_2(in_1[0]), .Carry_In(in_2[0]), .Sum(out_3[0]), .Carry_Out(full_adder_1_carry_out));
  Full_Adder full_adder_2 (
    .in_1(full_adder_1_carry_out), .in_2(in_1[1]), .Carry_In(in_2[1]), .Sum(out_3[1]),
    .Carry_Out(full_adder_2_carry_out));
  Full_Adder full_adder_3 (
    .in_1(full_adder_2_carry_out), .in_2(in_1[2]), .Carry_In(in_2[2]), .Sum(out_3[2]),
    .Carry_Out(full_adder_3_carry_out));
  Full_Adder full_adder_4 (
    .in_1(full_adder_3_carry_out), .in_2(in_1[3]), .Carry_In(in_2[3]), .Sum(out_3[3]),
    .Carry_Out(full_adder_4_carry_out));
  Full_Adder full_adder_5 (
    .in_1(full_adder_4_carry_out), .in_2(in_1[4]), .Carry_In(in_2[4]), .Sum(out_3[4]),
    .Carry_Out(full_adder_5_carry_out));
  Full_Adder full_adder_6 (
    .in_1(full_adder_5_carry_out), .in_2(in_1[5]), .Carry_In(in_2[5]), .Sum(out_3[5]),
    .Carry_Out(full_adder_6_carry_out));
  Full_Adder full_adder_7 (
    .in_1(full_adder_6_carry_out), .in_2(in_1[6]), .Carry_In(in_2[6]), .Sum(out_3[6]),
    .Carry_Out(full_adder_7_carry_out));
  Full_Adder full_adder_8 (
    .in_1(full_adder_7_carry_out), .in_2(in_1[7]), .Carry_In(in_2[7]), .Sum(out_3[7]),
    .Carry_Out(full_adder_8_carry_out));
  Full_Adder full_adder_9 (
    .in_1(full_adder_8_carry_out), .in_2(in_1[8]), .Carry_In(in_2[8]), .Sum(out_3[8]),
    .Carry_Out(full_adder_9_carry_out));
  Full_Adder full_adder_10 (
    .in_1(full_adder_9_carry_out), .in_2(in_1[9]), .Carry_In(in_2[9]), .Sum(out_3[9]),
    .Carry_Out(full_adder_10_carry_out));
  Full_Adder full_adder_11 (
    .in_1(full_adder_10_carry_out), .in_2(in_1[10]), .Carry_In(in_2[10]), .Sum(out_3[10]),
    .Carry_Out(full_adder_11_carry_out));
  Full_Adder full_adder_12 (
    .in_1(full_adder_11_carry_out), .in_2(in_1[11]), .Carry_In(in_2[11]), .Sum(out_3[11]),
    .Carry_Out(full_adder_12_carry_out));
  Full_Adder full_adder_13 (
    .in_1(full_adder_12_carry_out), .in_2(in_1[12]), .Carry_In(in_2[12]), .Sum(out_3[12]),
    .Carry_Out(full_adder_13_carry_out));
  Full_Adder full_adder_14 (
    .in_1(full_adder_13_carry_out), .in_2(in_1[13]), .Carry_In(in_2[13]), .Sum(out_3[13]),
    .Carry_Out(full_adder_14_carry_out));
  Full_Adder full_adder_15 (
    .in_1(full_adder_14_carry_out), .in_2(in_1[14]), .Carry_In(in_2[14]), .Sum(out_3[14]),
    .Carry_Out(full_adder_15_carry_out));
  Full_Adder full_adder_16 (
    .in_1(full_adder_15_carry_out), .in_2(in_1[15]), .Carry_In(in_2[15]), .Sum(out_3[15]),
    .Carry_Out(Carry_Out));
  not not_1 (not_1_out, in_1[15]);
  and and_1 (and_1_out, out_3[15], not_1_out, not_2_out);
  not not_2 (not_2_out, in_2[15]);
  not not_3 (not_3_out, out_3[15]);
  and and_2 (and_2_out, not_3_out, in_1[15], in_2[15]);
  or or_1 (Overflow, and_1_out, and_2_out);
endmodule

// Inv
module Additive_Inverse (
  input  [15:0] in_1,
  output [15:0] out_2,
  output Overflow
);

  wire [15:0] not_1_out;

  assign not_1_out = ~in_1;  // NOT_Gate not_1, 16 bits wide
  _16bit_Adder u_16bit_adder_1 (.in_1(not_1_out), .in_2(16'h1), .out_3(out_2), .Overflow(Overflow));  // open: Carry_Out
endmodule

// Sub
module _16bit_Subtractor (
  input  [15:0] in_1,
  input  [15:0] in_2,
  output [15:0] out_3,
  output Overflow
);

  wire additive_inverse_1_overflow, n16bit_adder_1_overflow;
  wire [15:0] additive_inverse_1_out_2;

  Additive_Inverse additive_inverse_1 (
    .in_1(in_2), .out_2(additive_inverse_1_out_2), .Overflow(additive_inverse_1_overflow));
  _16bit_Adder u_16bit_adder_1 (
    .in_1(in_1), .in_2(additive_inverse_1_out_2), .out_3(out_3), .Overflow(n16bit_adder_1_overflow));  // open: Carry_Out
  xor xor_1 (Overflow, n16bit_adder_1_overflow, additive_inverse_1_overflow);
endmodule

// Abs
module Absolute_Value (
  input  [15:0] in_1,
  output [15:0] out_2,
  output Is_it_negative
);

  wire not_1_out;
  wire [15:0] additive_inverse_1_out_2;

  Additive_Inverse additive_inverse_1 (.in_1(in_1), .out_2(additive_inverse_1_out_2));  // open: Overflow
  not not_1 (not_1_out, in_1[15]);
  Multiplexer #(.width(16), .enable("false")) multiplexer_1 (
    .in0(additive_inverse_1_out_2), .in1(in_1), .out(out_2), .sel(not_1_out));

  assign Is_it_negative = in_1[15];
endmodule

// Shift
module _15bit_Shifter (
  input  [15:0] in_1,
  input  [4:0] in_2,
  output [15:0] out_3,
  output Overflow
);

  wire [31:16] shifter_1_out;

  Shifter #(.width(32)) shifter_1 (.in({{16{1'b0}}, in_1}), .\dist (in_2), .out({shifter_1_out, out_3}));
  or or_1 (Overflow, out_3[15], shifter_1_out[16], shifter_1_out[17], shifter_1_out[18], shifter_1_out[19], shifter_1_out[20], shifter_1_out[21], shifter_1_out[22], shifter_1_out[23], shifter_1_out[24], shifter_1_out[25], shifter_1_out[26], shifter_1_out[27], shifter_1_out[28], shifter_1_out[29], shifter_1_out[30], shifter_1_out[31]);
endmodule

// Mulx1
module _16x1_Multiplier (
  input  in_1,
  input  [15:0] in_2,
  output [15:0] out_3
);

  and and_1 (out_3[0], in_2[0], in_1);
  and and_2 (out_3[1], in_2[1], in_1);
  and and_3 (out_3[2], in_2[2], in_1);
  and and_4 (out_3[3], in_2[3], in_1);
  and and_5 (out_3[4], in_2[4], in_1);
  and and_6 (out_3[5], in_2[5], in_1);
  and and_7 (out_3[6], in_2[6], in_1);
  and and_8 (out_3[7], in_2[7], in_1);
  and and_9 (out_3[8], in_2[8], in_1);
  and and_10 (out_3[9], in_2[9], in_1);
  and and_11 (out_3[10], in_2[10], in_1);
  and and_12 (out_3[11], in_2[11], in_1);
  and and_13 (out_3[12], in_2[12], in_1);
  and and_14 (out_3[13], in_2[13], in_1);
  and and_15 (out_3[14], in_2[14], in_1);
  and and_16 (out_3[15], in_2[15], in_1);
endmodule

// Mult
module _16bit_Multiplier (
  input  [15:0] in_1,
  input  [15:0] in_2,
  output [15:0] out_3,
  output Overflow
);

  wire absolute_value_1_is_it_negative, absolute_value_2_is_it_negative, additive_inverse_1_overflow,
       and_1_out, n15bit_shifter_1_overflow, n15bit_shifter_2_overflow, n15bit_shifter_3_overflow,
       n15bit_shifter_4_overflow, n15bit_shifter_5_overflow, n15bit_shifter_6_overflow,
       n15bit_shifter_7_overflow, n15bit_shifter_8_overflow, n15bit_shifter_9_overflow,
       n15bit_shifter_10_overflow, n15bit_shifter_11_overflow, n15bit_shifter_12_overflow,
       n15bit_shifter_13_overflow, n15bit_shifter_14_overflow, n15bit_shifter_15_overflow, not_1_out,
       or_1_out, xor_1_out;
  wire [15:0] absolute_value_1_out_2, absolute_value_2_out_2, additive_inverse_1_out_2,
       n15bit_shifter_1_out_3, n15bit_shifter_2_out_3, n15bit_shifter_3_out_3, n15bit_shifter_4_out_3,
       n15bit_shifter_5_out_3, n15bit_shifter_6_out_3, n15bit_shifter_7_out_3, n15bit_shifter_8_out_3,
       n15bit_shifter_9_out_3, n15bit_shifter_10_out_3, n15bit_shifter_11_out_3, n15bit_shifter_12_out_3,
       n15bit_shifter_13_out_3, n15bit_shifter_14_out_3, n15bit_shifter_15_out_3, n16bit_adder_1_out_3,
       n16bit_adder_2_out_3, n16bit_adder_3_out_3, n16bit_adder_4_out_3, n16bit_adder_5_out_3,
       n16bit_adder_6_out_3, n16bit_adder_7_out_3, n16bit_adder_8_out_3, n16bit_adder_9_out_3,
       n16bit_adder_10_out_3, n16bit_adder_11_out_3, n16bit_adder_12_out_3, n16bit_adder_13_out_3,
       n16bit_adder_14_out_3, n16bit_adder_15_out_3, n16x1_multiplier_1_out_3, n16x1_multiplier_2_out_3,
       n16x1_multiplier_3_out_3, n16x1_multiplier_4_out_3, n16x1_multiplier_5_out_3,
       n16x1_multiplier_6_out_3, n16x1_multiplier_7_out_3, n16x1_multiplier_8_out_3,
       n16x1_multiplier_9_out_3, n16x1_multiplier_10_out_3, n16x1_multiplier_11_out_3,
       n16x1_multiplier_12_out_3, n16x1_multiplier_13_out_3, n16x1_multiplier_14_out_3,
       n16x1_multiplier_15_out_3, n16x1_multiplier_16_out_3;

  Absolute_Value absolute_value_1 (
    .in_1(in_2), .out_2(absolute_value_1_out_2), .Is_it_negative(absolute_value_1_is_it_negative));
  Absolute_Value absolute_value_2 (
    .in_1(in_1), .out_2(absolute_value_2_out_2), .Is_it_negative(absolute_value_2_is_it_negative));
  _16x1_Multiplier u_16x1_multiplier_1 (
    .in_1(absolute_value_1_out_2[0]), .in_2(absolute_value_2_out_2), .out_3(n16x1_multiplier_1_out_3));
  _16x1_Multiplier u_16x1_multiplier_2 (
    .in_1(absolute_value_1_out_2[1]), .in_2(absolute_value_2_out_2), .out_3(n16x1_multiplier_2_out_3));
  _16x1_Multiplier u_16x1_multiplier_3 (
    .in_1(absolute_value_1_out_2[2]), .in_2(absolute_value_2_out_2), .out_3(n16x1_multiplier_3_out_3));
  _16x1_Multiplier u_16x1_multiplier_4 (
    .in_1(absolute_value_1_out_2[3]), .in_2(absolute_value_2_out_2), .out_3(n16x1_multiplier_4_out_3));
  _16x1_Multiplier u_16x1_multiplier_5 (
    .in_1(absolute_value_1_out_2[4]), .in_2(absolute_value_2_out_2), .out_3(n16x1_multiplier_5_out_3));
  _16x1_Multiplier u_16x1_multiplier_6 (
    .in_1(absolute_value_1_out_2[5]), .in_2(absolute_value_2_out_2), .out_3(n16x1_multiplier_6_out_3));
  _16x1_Multiplier u_16x1_multiplier_7 (
    .in_1(absolute_value_1_out_2[6]), .in_2(absolute_value_2_out_2), .out_3(n16x1_multiplier_7_out_3));
  _16x1_Multiplier u_16x1_multiplier_8 (
    .in_1(absolute_value_1_out_2[7]), .in_2(absolute_value_2_out_2), .out_3(n16x1_multiplier_8_out_3));
  _16x1_Multiplier u_16x1_multiplier_9 (
    .in_1(absolute_value_1_out_2[8]), .in_2(absolute_value_2_out_2), .out_3(n16x1_multiplier_9_out_3));
  _16x1_Multiplier u_16x1_multiplier_10 (
    .in_1(absolute_value_1_out_2[9]), .in_2(absolute_value_2_out_2), .out_3(n16x1_multiplier_10_out_3));
  _16x1_Multiplier u_16x1_multiplier_11 (
    .in_1(absolute_value_1_out_2[10]), .in_2(absolute_value_2_out_2), .out_3(n16x1_multiplier_11_out_3));
  _16x1_Multiplier u_16x1_multiplier_12 (
    .in_1(absolute_value_1_out_2[11]), .in_2(absolute_value_2_out_2), .out_3(n16x1_multiplier_12_out_3));
  _16x1_Multiplier u_16x1_multiplier_13 (
    .in_1(absolute_value_1_out_2[12]), .in_2(absolute_value_2_out_2), .out_3(n16x1_multiplier_13_out_3));
  _16x1_Multiplier u_16x1_multiplier_14 (
    .in_1(absolute_value_1_out_2[13]), .in_2(absolute_value_2_out_2), .out_3(n16x1_multiplier_14_out_3));
  _16x1_Multiplier u_16x1_multiplier_15 (
    .in_1(absolute_value_1_out_2[14]), .in_2(absolute_value_2_out_2), .out_3(n16x1_multiplier_15_out_3));
  _16x1_Multiplier u_16x1_multiplier_16 (
    .in_1(absolute_value_1_out_2[15]), .in_2(absolute_value_2_out_2), .out_3(n16x1_multiplier_16_out_3));
  _15bit_Shifter u_15bit_shifter_1 (
    .in_1(n16x1_multiplier_2_out_3), .in_2(5'b00001), .out_3(n15bit_shifter_1_out_3),
    .Overflow(n15bit_shifter_1_overflow));
  _15bit_Shifter u_15bit_shifter_2 (
    .in_1(n16x1_multiplier_3_out_3), .in_2(5'b00010), .out_3(n15bit_shifter_2_out_3),
    .Overflow(n15bit_shifter_2_overflow));
  _15bit_Shifter u_15bit_shifter_3 (
    .in_1(n16x1_multiplier_4_out_3), .in_2(5'b00011), .out_3(n15bit_shifter_3_out_3),
    .Overflow(n15bit_shifter_3_overflow));
  _15bit_Shifter u_15bit_shifter_4 (
    .in_1(n16x1_multiplier_5_out_3), .in_2(5'b00100), .out_3(n15bit_shifter_4_out_3),
    .Overflow(n15bit_shifter_4_overflow));
  _15bit_Shifter u_15bit_shifter_5 (
    .in_1(n16x1_multiplier_6_out_3), .in_2(5'b00101), .out_3(n15bit_shifter_5_out_3),
    .Overflow(n15bit_shifter_5_overflow));
  _15bit_Shifter u_15bit_shifter_6 (
    .in_1(n16x1_multiplier_7_out_3), .in_2(5'b00110), .out_3(n15bit_shifter_6_out_3),
    .Overflow(n15bit_shifter_6_overflow));
  _15bit_Shifter u_15bit_shifter_7 (
    .in_1(n16x1_multiplier_8_out_3), .in_2(5'b00111), .out_3(n15bit_shifter_7_out_3),
    .Overflow(n15bit_shifter_7_overflow));
  _15bit_Shifter u_15bit_shifter_8 (
    .in_1(n16x1_multiplier_9_out_3), .in_2(5'b01000), .out_3(n15bit_shifter_8_out_3),
    .Overflow(n15bit_shifter_8_overflow));
  _15bit_Shifter u_15bit_shifter_9 (
    .in_1(n16x1_multiplier_10_out_3), .in_2(5'b01001), .out_3(n15bit_shifter_9_out_3),
    .Overflow(n15bit_shifter_9_overflow));
  _15bit_Shifter u_15bit_shifter_10 (
    .in_1(n16x1_multiplier_11_out_3), .in_2(5'b10000), .out_3(n15bit_shifter_10_out_3),
    .Overflow(n15bit_shifter_10_overflow));
  _15bit_Shifter u_15bit_shifter_11 (
    .in_1(n16x1_multiplier_12_out_3), .in_2(5'b10001), .out_3(n15bit_shifter_11_out_3),
    .Overflow(n15bit_shifter_11_overflow));
  _15bit_Shifter u_15bit_shifter_12 (
    .in_1(n16x1_multiplier_13_out_3), .in_2(5'b10010), .out_3(n15bit_shifter_12_out_3),
    .Overflow(n15bit_shifter_12_overflow));
  _15bit_Shifter u_15bit_shifter_13 (
    .in_1(n16x1_multiplier_14_out_3), .in_2(5'b10011), .out_3(n15bit_shifter_13_out_3),
    .Overflow(n15bit_shifter_13_overflow));
  _15bit_Shifter u_15bit_shifter_14 (
    .in_1(n16x1_multiplier_15_out_3), .in_2(5'b10100), .out_3(n15bit_shifter_14_out_3),
    .Overflow(n15bit_shifter_14_overflow));
  _15bit_Shifter u_15bit_shifter_15 (
    .in_1(n16x1_multiplier_16_out_3), .in_2(5'b10101), .out_3(n15bit_shifter_15_out_3),
    .Overflow(n15bit_shifter_15_overflow));
  xor xor_1 (xor_1_out, absolute_value_2_is_it_negative, absolute_value_1_is_it_negative);
  _16bit_Adder u_16bit_adder_1 (
    .in_1(n16x1_multiplier_1_out_3), .in_2(n15bit_shifter_1_out_3), .out_3(n16bit_adder_1_out_3));  // open: Carry_Out, Overflow
  _16bit_Adder u_16bit_adder_2 (
    .in_1(n16bit_adder_1_out_3), .in_2(n15bit_shifter_2_out_3), .out_3(n16bit_adder_2_out_3));  // open: Carry_Out, Overflow
  _16bit_Adder u_16bit_adder_3 (
    .in_1(n16bit_adder_2_out_3), .in_2(n15bit_shifter_3_out_3), .out_3(n16bit_adder_3_out_3));  // open: Carry_Out, Overflow
  _16bit_Adder u_16bit_adder_4 (
    .in_1(n16bit_adder_3_out_3), .in_2(n15bit_shifter_4_out_3), .out_3(n16bit_adder_4_out_3));  // open: Carry_Out, Overflow
  _16bit_Adder u_16bit_adder_5 (
    .in_1(n16bit_adder_4_out_3), .in_2(n15bit_shifter_5_out_3), .out_3(n16bit_adder_5_out_3));  // open: Carry_Out, Overflow
  _16bit_Adder u_16bit_adder_6 (
    .in_1(n16bit_adder_5_out_3), .in_2(n15bit_shifter_6_out_3), .out_3(n16bit_adder_6_out_3));  // open: Carry_Out, Overflow
  _16bit_Adder u_16bit_adder_7 (
    .in_1(n16bit_adder_6_out_3), .in_2(n15bit_shifter_7_out_3), .out_3(n16bit_adder_7_out_3));  // open: Carry_Out, Overflow
  _16bit_Adder u_16bit_adder_8 (
    .in_1(n16bit_adder_7_out_3), .in_2(n15bit_shifter_8_out_3), .out_3(n16bit_adder_8_out_3));  // open: Carry_Out, Overflow
  _16bit_Adder u_16bit_adder_9 (
    .in_1(n16bit_adder_8_out_3), .in_2(n15bit_shifter_9_out_3), .out_3(n16bit_adder_9_out_3));  // open: Carry_Out, Overflow
  _16bit_Adder u_16bit_adder_10 (
    .in_1(n16bit_adder_9_out_3), .in_2(n15bit_shifter_10_out_3), .out_3(n16bit_adder_10_out_3));  // open: Carry_Out, Overflow
  _16bit_Adder u_16bit_adder_11 (
    .in_1(n16bit_adder_10_out_3), .in_2(n15bit_shifter_11_out_3), .out_3(n16bit_adder_11_out_3));  // open: Carry_Out, Overflow
  _16bit_Adder u_16bit_adder_12 (
    .in_1(n16bit_adder_11_out_3), .in_2(n15bit_shifter_12_out_3), .out_3(n16bit_adder_12_out_3));  // open: Carry_Out, Overflow
  _16bit_Adder u_16bit_adder_13 (
    .in_1(n16bit_adder_14_out_3), .in_2(n15bit_shifter_14_out_3), .out_3(n16bit_adder_13_out_3));  // open: Carry_Out, Overflow
  _16bit_Adder u_16bit_adder_14 (
    .in_1(n16bit_adder_12_out_3), .in_2(n15bit_shifter_13_out_3), .out_3(n16bit_adder_14_out_3));  // open: Carry_Out, Overflow
  _16bit_Adder u_16bit_adder_15 (
    .in_1(n16bit_adder_13_out_3), .in_2(n15bit_shifter_15_out_3), .out_3(n16bit_adder_15_out_3));  // open: Carry_Out, Overflow
  Additive_Inverse additive_inverse_1 (
    .in_1(n16bit_adder_15_out_3), .out_2(additive_inverse_1_out_2), .Overflow(additive_inverse_1_overflow));
  or or_1 (or_1_out, n15bit_shifter_1_overflow, n15bit_shifter_2_overflow, n15bit_shifter_3_overflow, n15bit_shifter_4_overflow, n15bit_shifter_5_overflow, n15bit_shifter_6_overflow, n15bit_shifter_7_overflow, n15bit_shifter_8_overflow, n15bit_shifter_9_overflow, n15bit_shifter_10_overflow, n15bit_shifter_11_overflow, n15bit_shifter_12_overflow, n15bit_shifter_13_overflow, n15bit_shifter_14_overflow, n15bit_shifter_15_overflow);
  Multiplexer #(.width(16), .enable("false")) multiplexer_1 (
    .in0(n16bit_adder_15_out_3), .in1(additive_inverse_1_out_2), .out(out_3), .sel(xor_1_out));
  not not_1 (not_1_out, xor_1_out);
  and and_1 (and_1_out, additive_inverse_1_overflow, not_1_out);
  or or_2 (Overflow, and_1_out, or_1_out);
endmodule

// Shift
module _16bit_Shifter (
  input  [15:0] in_1,
  input  [4:0] in_2,
  output [15:0] out_3,
  output Overflow
);

  wire [31:16] shifter_1_out;

  Shifter #(.width(32)) shifter_1 (.in({{16{1'b0}}, in_1}), .\dist (in_2), .out({shifter_1_out, out_3}));
  or or_1 (Overflow, shifter_1_out[16], shifter_1_out[17], shifter_1_out[18], shifter_1_out[19], shifter_1_out[20], shifter_1_out[21], shifter_1_out[22], shifter_1_out[23], shifter_1_out[24], shifter_1_out[25], shifter_1_out[26], shifter_1_out[27], shifter_1_out[28], shifter_1_out[29], shifter_1_out[30], shifter_1_out[31]);
endmodule

// Div
module _16bit_Divider (
  input  [15:0] in_1,
  input  [15:0] in_2,
  input  Option,
  output [15:0] out_4,
  output Overflow
);

  wire absolute_value_1_is_it_negative, absolute_value_2_is_it_negative, additive_inverse_1_overflow,
       multiplexer_19_out, n15bit_shifter_1_overflow, n15bit_shifter_2_overflow, n15bit_shifter_3_overflow,
       n15bit_shifter_4_overflow, n15bit_shifter_5_overflow, n15bit_shifter_6_overflow,
       n15bit_shifter_7_overflow, n15bit_shifter_8_overflow, n15bit_shifter_9_overflow,
       n15bit_shifter_10_overflow, n15bit_shifter_11_overflow, n15bit_shifter_12_overflow,
       n15bit_shifter_13_overflow, n16bit_shifter_1_overflow, n16bit_shifter_2_overflow, not_1_out,
       not_2_out, xor_1_out;
  wire [15:0] absolute_value_1_out_2, absolute_value_2_out_2, additive_inverse_1_out_2, multiplexer_1_out,
       multiplexer_2_out, multiplexer_3_out, multiplexer_4_out, multiplexer_5_out, multiplexer_6_out,
       multiplexer_7_out, multiplexer_8_out, multiplexer_9_out, multiplexer_10_out, multiplexer_11_out,
       multiplexer_12_out, multiplexer_13_out, multiplexer_14_out, multiplexer_15_out, multiplexer_16_out,
       multiplexer_17_out, multiplexer_18_out, multiplexer_20_out, multiplexer_21_out, multiplexer_22_out,
       multiplexer_23_out, multiplexer_24_out, multiplexer_25_out, multiplexer_26_out, multiplexer_27_out,
       multiplexer_28_out, multiplexer_29_out, multiplexer_30_out, multiplexer_31_out, multiplexer_33_out,
       multiplexer_34_out, n15bit_shifter_1_out_3, n15bit_shifter_2_out_3, n15bit_shifter_3_out_3,
       n15bit_shifter_4_out_3, n15bit_shifter_5_out_3, n15bit_shifter_6_out_3, n15bit_shifter_7_out_3,
       n15bit_shifter_8_out_3, n15bit_shifter_9_out_3, n15bit_shifter_10_out_3, n15bit_shifter_11_out_3,
       n15bit_shifter_12_out_3, n15bit_shifter_13_out_3, n16bit_shifter_1_out_3, n16bit_shifter_2_out_3,
       n16bit_subtractor_1_out_3, n16bit_subtractor_2_out_3, n16bit_subtractor_3_out_3,
       n16bit_subtractor_4_out_3, n16bit_subtractor_5_out_3, n16bit_subtractor_6_out_3,
       n16bit_subtractor_7_out_3, n16bit_subtractor_8_out_3, n16bit_subtractor_9_out_3,
       n16bit_subtractor_10_out_3, n16bit_subtractor_11_out_3, n16bit_subtractor_12_out_3,
       n16bit_subtractor_13_out_3, n16bit_subtractor_14_out_3, n16bit_subtractor_15_out_3,
       n16bit_subtractor_16_out_3, nor_1_out;

  Absolute_Value absolute_value_1 (
    .in_1(in_1), .out_2(absolute_value_1_out_2), .Is_it_negative(absolute_value_1_is_it_negative));
  Absolute_Value absolute_value_2 (
    .in_1(in_2), .out_2(absolute_value_2_out_2), .Is_it_negative(absolute_value_2_is_it_negative));
  _16bit_Shifter u_16bit_shifter_1 (
    .in_1(absolute_value_2_out_2), .in_2(5'b10101), .out_3(n16bit_shifter_1_out_3),
    .Overflow(n16bit_shifter_1_overflow));
  _15bit_Shifter u_15bit_shifter_1 (
    .in_1(absolute_value_2_out_2), .in_2(5'b10100), .out_3(n15bit_shifter_1_out_3),
    .Overflow(n15bit_shifter_1_overflow));
  _15bit_Shifter u_15bit_shifter_2 (
    .in_1(absolute_value_2_out_2), .in_2(5'b10011), .out_3(n15bit_shifter_2_out_3),
    .Overflow(n15bit_shifter_2_overflow));
  _15bit_Shifter u_15bit_shifter_3 (
    .in_1(absolute_value_2_out_2), .in_2(5'b10010), .out_3(n15bit_shifter_3_out_3),
    .Overflow(n15bit_shifter_3_overflow));
  _15bit_Shifter u_15bit_shifter_4 (
    .in_1(absolute_value_2_out_2), .in_2(5'b10001), .out_3(n15bit_shifter_4_out_3),
    .Overflow(n15bit_shifter_4_overflow));
  Multiplexer #(.width(16), .enable("false")) multiplexer_1 (
    .in0(n16bit_shifter_1_out_3), .in1({16{1'b0}}), .out(multiplexer_1_out), .sel(n16bit_shifter_1_overflow));
  Multiplexer #(.width(16), .enable("false")) multiplexer_2 (
    .in0(n15bit_shifter_1_out_3), .in1({16{1'b0}}), .out(multiplexer_2_out), .sel(n15bit_shifter_1_overflow));
  Multiplexer #(.width(16), .enable("false")) multiplexer_3 (
    .in0(n15bit_shifter_2_out_3), .in1({16{1'b0}}), .out(multiplexer_3_out), .sel(n15bit_shifter_2_overflow));
  Multiplexer #(.width(16), .enable("false")) multiplexer_4 (
    .in0(n15bit_shifter_3_out_3), .in1({16{1'b0}}), .out(multiplexer_4_out), .sel(n15bit_shifter_3_overflow));
  _15bit_Shifter u_15bit_shifter_5 (
    .in_1(absolute_value_2_out_2), .in_2(5'b10000), .out_3(n15bit_shifter_5_out_3),
    .Overflow(n15bit_shifter_5_overflow));
  _15bit_Shifter u_15bit_shifter_6 (
    .in_1(absolute_value_2_out_2), .in_2(5'b01001), .out_3(n15bit_shifter_6_out_3),
    .Overflow(n15bit_shifter_6_overflow));
  _15bit_Shifter u_15bit_shifter_7 (
    .in_1(absolute_value_2_out_2), .in_2(5'b01000), .out_3(n15bit_shifter_7_out_3),
    .Overflow(n15bit_shifter_7_overflow));
  _16bit_Shifter u_16bit_shifter_2 (
    .in_1(absolute_value_2_out_2), .in_2(5'b00111), .out_3(n16bit_shifter_2_out_3),
    .Overflow(n16bit_shifter_2_overflow));
  _16bit_Subtractor u_16bit_subtractor_1 (
    .in_1(absolute_value_1_out_2), .in_2(multiplexer_1_out), .out_3(n16bit_subtractor_1_out_3));  // open: Overflow
  _16bit_Subtractor u_16bit_subtractor_2 (
    .in_1(multiplexer_13_out), .in_2(multiplexer_2_out), .out_3(n16bit_subtractor_2_out_3));  // open: Overflow
  _16bit_Subtractor u_16bit_subtractor_3 (
    .in_1(multiplexer_14_out), .in_2(multiplexer_3_out), .out_3(n16bit_subtractor_3_out_3));  // open: Overflow
  _16bit_Subtractor u_16bit_subtractor_4 (
    .in_1(multiplexer_15_out), .in_2(multiplexer_4_out), .out_3(n16bit_subtractor_4_out_3));  // open: Overflow
  Multiplexer #(.width(16), .enable("false")) multiplexer_5 (
    .in0(n15bit_shifter_4_out_3), .in1({16{1'b0}}), .out(multiplexer_5_out), .sel(n15bit_shifter_4_overflow));
  Multiplexer #(.width(16), .enable("false")) multiplexer_6 (
    .in0(n15bit_shifter_5_out_3), .in1({16{1'b0}}), .out(multiplexer_6_out), .sel(n15bit_shifter_5_overflow));
  Multiplexer #(.width(16), .enable("false")) multiplexer_7 (
    .in0(n15bit_shifter_6_out_3), .in1({16{1'b0}}), .out(multiplexer_7_out), .sel(n15bit_shifter_6_overflow));
  Multiplexer #(.width(16), .enable("false")) multiplexer_8 (
    .in0(n15bit_shifter_7_out_3), .in1({16{1'b0}}), .out(multiplexer_8_out), .sel(n15bit_shifter_7_overflow));
  _15bit_Shifter u_15bit_shifter_8 (
    .in_1(absolute_value_2_out_2), .in_2(5'b00110), .out_3(n15bit_shifter_8_out_3),
    .Overflow(n15bit_shifter_8_overflow));
  _15bit_Shifter u_15bit_shifter_9 (
    .in_1(absolute_value_2_out_2), .in_2(5'b00101), .out_3(n15bit_shifter_9_out_3),
    .Overflow(n15bit_shifter_9_overflow));
  _15bit_Shifter u_15bit_shifter_10 (
    .in_1(absolute_value_2_out_2), .in_2(5'b00100), .out_3(n15bit_shifter_10_out_3),
    .Overflow(n15bit_shifter_10_overflow));
  _15bit_Shifter u_15bit_shifter_11 (
    .in_1(absolute_value_2_out_2), .in_2(5'b00011), .out_3(n15bit_shifter_11_out_3),
    .Overflow(n15bit_shifter_11_overflow));
  xor xor_1 (xor_1_out, absolute_value_1_is_it_negative, absolute_value_2_is_it_negative);
  _16bit_Subtractor u_16bit_subtractor_5 (
    .in_1(multiplexer_20_out), .in_2(multiplexer_5_out), .out_3(n16bit_subtractor_5_out_3));  // open: Overflow
  _16bit_Subtractor u_16bit_subtractor_6 (
    .in_1(multiplexer_21_out), .in_2(multiplexer_6_out), .out_3(n16bit_subtractor_6_out_3));  // open: Overflow
  _16bit_Subtractor u_16bit_subtractor_7 (
    .in_1(multiplexer_22_out), .in_2(multiplexer_7_out), .out_3(n16bit_subtractor_7_out_3));  // open: Overflow
  _16bit_Subtractor u_16bit_subtractor_8 (
    .in_1(multiplexer_23_out), .in_2(multiplexer_8_out), .out_3(n16bit_subtractor_8_out_3));  // open: Overflow
  Multiplexer #(.width(16), .enable("false")) multiplexer_9 (
    .in0(n16bit_shifter_2_out_3), .in1({16{1'b0}}), .out(multiplexer_9_out), .sel(n16bit_shifter_2_overflow));
  Multiplexer #(.width(16), .enable("false")) multiplexer_10 (
    .in0(n15bit_shifter_8_out_3), .in1({16{1'b0}}), .out(multiplexer_10_out), .sel(n15bit_shifter_8_overflow));
  Multiplexer #(.width(16), .enable("false")) multiplexer_11 (
    .in0(n15bit_shifter_9_out_3), .in1({16{1'b0}}), .out(multiplexer_11_out), .sel(n15bit_shifter_9_overflow));
  Multiplexer #(.width(16), .enable("false")) multiplexer_12 (
    .in0(n15bit_shifter_10_out_3), .in1({16{1'b0}}), .out(multiplexer_12_out),
    .sel(n15bit_shifter_10_overflow));
  _15bit_Shifter u_15bit_shifter_12 (
    .in_1(absolute_value_2_out_2), .in_2(5'b00010), .out_3(n15bit_shifter_12_out_3),
    .Overflow(n15bit_shifter_12_overflow));
  _15bit_Shifter u_15bit_shifter_13 (
    .in_1(absolute_value_2_out_2), .in_2(5'b00001), .out_3(n15bit_shifter_13_out_3),
    .Overflow(n15bit_shifter_13_overflow));
  Multiplexer #(.width(16), .enable("false")) multiplexer_13 (
    .in0(n16bit_subtractor_1_out_3), .in1(absolute_value_1_out_2), .out(multiplexer_13_out),
    .sel(n16bit_subtractor_1_out_3[15]));
  Multiplexer #(.width(16), .enable("false")) multiplexer_14 (
    .in0(n16bit_subtractor_2_out_3), .in1(multiplexer_13_out), .out(multiplexer_14_out),
    .sel(n16bit_subtractor_2_out_3[15]));
  Multiplexer #(.width(16), .enable("false")) multiplexer_15 (
    .in0(n16bit_subtractor_3_out_3), .in1(multiplexer_14_out), .out(multiplexer_15_out),
    .sel(n16bit_subtractor_3_out_3[15]));
  _16bit_Subtractor u_16bit_subtractor_9 (
    .in_1(multiplexer_24_out), .in_2(multiplexer_9_out), .out_3(n16bit_subtractor_9_out_3));  // open: Overflow
  _16bit_Subtractor u_16bit_subtractor_10 (
    .in_1(multiplexer_25_out), .in_2(multiplexer_10_out), .out_3(n16bit_subtractor_10_out_3));  // open: Overflow
  _16bit_Subtractor u_16bit_subtractor_11 (
    .in_1(multiplexer_26_out), .in_2(multiplexer_11_out), .out_3(n16bit_subtractor_11_out_3));  // open: Overflow
  _16bit_Subtractor u_16bit_subtractor_12 (
    .in_1(multiplexer_27_out), .in_2(multiplexer_12_out), .out_3(n16bit_subtractor_12_out_3));  // open: Overflow
  Multiplexer #(.width(16), .enable("false")) multiplexer_16 (
    .in0(n15bit_shifter_11_out_3), .in1({16{1'b0}}), .out(multiplexer_16_out),
    .sel(n15bit_shifter_11_overflow));
  Multiplexer #(.width(16), .enable("false")) multiplexer_17 (
    .in0(n15bit_shifter_12_out_3), .in1({16{1'b0}}), .out(multiplexer_17_out),
    .sel(n15bit_shifter_12_overflow));
  Multiplexer #(.width(16), .enable("false")) multiplexer_18 (
    .in0(n15bit_shifter_13_out_3), .in1({16{1'b0}}), .out(multiplexer_18_out),
    .sel(n15bit_shifter_13_overflow));
  Multiplexer #(.enable("false")) multiplexer_19 (
    .in0(absolute_value_1_is_it_negative), .in1(xor_1_out), .out(multiplexer_19_out), .sel(not_1_out));
  not not_1 (not_1_out, Option);
  Multiplexer #(.width(16), .enable("false")) multiplexer_20 (
    .in0(n16bit_subtractor_4_out_3), .in1(multiplexer_15_out), .out(multiplexer_20_out),
    .sel(n16bit_subtractor_4_out_3[15]));
  Multiplexer #(.width(16), .enable("false")) multiplexer_21 (
    .in0(n16bit_subtractor_5_out_3), .in1(multiplexer_20_out), .out(multiplexer_21_out),
    .sel(n16bit_subtractor_5_out_3[15]));
  Multiplexer #(.width(16), .enable("false")) multiplexer_22 (
    .in0(n16bit_subtractor_6_out_3), .in1(multiplexer_21_out), .out(multiplexer_22_out),
    .sel(n16bit_subtractor_6_out_3[15]));
  Multiplexer #(.width(16), .enable("false")) multiplexer_23 (
    .in0(n16bit_subtractor_7_out_3), .in1(multiplexer_22_out), .out(multiplexer_23_out),
    .sel(n16bit_subtractor_7_out_3[15]));
  _16bit_Subtractor u_16bit_subtractor_13 (
    .in_1(multiplexer_28_out), .in_2(multiplexer_16_out), .out_3(n16bit_subtractor_13_out_3));  // open: Overflow
  _16bit_Subtractor u_16bit_subtractor_14 (
    .in_1(multiplexer_29_out), .in_2(multiplexer_17_out), .out_3(n16bit_subtractor_14_out_3));  // open: Overflow
  _16bit_Subtractor u_16bit_subtractor_15 (
    .in_1(multiplexer_30_out), .in_2(multiplexer_18_out), .out_3(n16bit_subtractor_15_out_3));  // open: Overflow
  _16bit_Subtractor u_16bit_subtractor_16 (
    .in_1(multiplexer_31_out), .in_2(absolute_value_2_out_2), .out_3(n16bit_subtractor_16_out_3));  // open: Overflow
  nor nor_1 (nor_1_out[0], n16bit_subtractor_1_out_3[15], n16bit_shifter_1_overflow);
  nor nor_2 (nor_1_out[1], n16bit_subtractor_2_out_3[15], n15bit_shifter_1_overflow);
  nor nor_3 (nor_1_out[2], n16bit_subtractor_3_out_3[15], n15bit_shifter_2_overflow);
  nor nor_4 (nor_1_out[3], n16bit_subtractor_4_out_3[15], n15bit_shifter_3_overflow);
  Multiplexer #(.width(16), .enable("false")) multiplexer_24 (
    .in0(n16bit_subtractor_8_out_3), .in1(multiplexer_23_out), .out(multiplexer_24_out),
    .sel(n16bit_subtractor_8_out_3[15]));
  Multiplexer #(.width(16), .enable("false")) multiplexer_25 (
    .in0(n16bit_subtractor_9_out_3), .in1(multiplexer_24_out), .out(multiplexer_25_out),
    .sel(n16bit_subtractor_9_out_3[15]));
  Multiplexer #(.width(16), .enable("false")) multiplexer_26 (
    .in0(n16bit_subtractor_10_out_3), .in1(multiplexer_25_out), .out(multiplexer_26_out),
    .sel(n16bit_subtractor_10_out_3[15]));
  Multiplexer #(.width(16), .enable("false")) multiplexer_27 (
    .in0(n16bit_subtractor_11_out_3), .in1(multiplexer_26_out), .out(multiplexer_27_out),
    .sel(n16bit_subtractor_11_out_3[15]));
  Additive_Inverse additive_inverse_1 (
    .in_1(multiplexer_34_out), .out_2(additive_inverse_1_out_2), .Overflow(additive_inverse_1_overflow));
  nor nor_5 (nor_1_out[4], n16bit_subtractor_5_out_3[15], n15bit_shifter_4_overflow);
  nor nor_6 (nor_1_out[5], n16bit_subtractor_6_out_3[15], n15bit_shifter_5_overflow);
  nor nor_7 (nor_1_out[6], n16bit_subtractor_7_out_3[15], n15bit_shifter_6_overflow);
  nor nor_8 (nor_1_out[7], n16bit_subtractor_8_out_3[15], n15bit_shifter_7_overflow);
  Multiplexer #(.width(16), .enable("false")) multiplexer_28 (
    .in0(n16bit_subtractor_12_out_3), .in1(multiplexer_27_out), .out(multiplexer_28_out),
    .sel(n16bit_subtractor_12_out_3[15]));
  Multiplexer #(.width(16), .enable("false")) multiplexer_29 (
    .in0(n16bit_subtractor_13_out_3), .in1(multiplexer_28_out), .out(multiplexer_29_out),
    .sel(n16bit_subtractor_13_out_3[15]));
  Multiplexer #(.width(16), .enable("false")) multiplexer_30 (
    .in0(n16bit_subtractor_14_out_3), .in1(multiplexer_29_out), .out(multiplexer_30_out),
    .sel(n16bit_subtractor_14_out_3[15]));
  Multiplexer #(.width(16), .enable("false")) multiplexer_31 (
    .in0(n16bit_subtractor_15_out_3), .in1(multiplexer_30_out), .out(multiplexer_31_out),
    .sel(n16bit_subtractor_15_out_3[15]));
  Multiplexer #(.width(16), .enable("false")) multiplexer_32 (
    .in0(multiplexer_34_out), .in1(additive_inverse_1_out_2), .out(out_4), .sel(multiplexer_19_out));
  not not_2 (not_2_out, multiplexer_19_out);
  nor nor_9 (nor_1_out[8], n16bit_subtractor_9_out_3[15], n16bit_shifter_2_overflow);
  nor nor_10 (nor_1_out[9], n16bit_subtractor_10_out_3[15], n15bit_shifter_8_overflow);
  nor nor_11 (nor_1_out[10], n16bit_subtractor_11_out_3[15], n15bit_shifter_9_overflow);
  nor nor_12 (nor_1_out[11], n16bit_subtractor_12_out_3[15], n15bit_shifter_10_overflow);
  Multiplexer #(.width(16), .enable("false")) multiplexer_33 (
    .in0(n16bit_subtractor_16_out_3), .in1(multiplexer_31_out), .out(multiplexer_33_out),
    .sel(n16bit_subtractor_16_out_3[15]));
  and and_1 (Overflow, additive_inverse_1_overflow, not_2_out);
  nor nor_13 (nor_1_out[12], n16bit_subtractor_13_out_3[15], n15bit_shifter_11_overflow);
  nor nor_14 (nor_1_out[13], n16bit_subtractor_14_out_3[15], n15bit_shifter_12_overflow);
  nor nor_15 (nor_1_out[14], n16bit_subtractor_15_out_3[15], n15bit_shifter_13_overflow);
  not not_3 (nor_1_out[15], n16bit_subtractor_16_out_3[15]);
  Multiplexer #(.width(16), .enable("false")) multiplexer_34 (
    .in0(nor_1_out), .in1(multiplexer_33_out), .out(multiplexer_34_out), .sel(Option));
endmodule
