// Logisim project Main.circ as structural Verilog: 5 circuits, main circuit main
module main (
  input  [15:0] in_1,
  output [15:0] out_2,
  output [15:0] out_3
);

  wire alu, ALU_division_by_zero, ALU_overflow, and_1_out, arthm_error, clock_1_out, clock_2_out,
       clock_3_out, clock_4_out, clock_5_out, Control_end, Control_load_ram, Control_store_acc,
       Control_store_ram, load_ram, not_1_out, phase_0, phase_1, print, run, select_acc, select_pc,
       select_ram, store_acc, store_ram;
  wire [2:0] op;
  wire [5:0] flags;
  wire [7:0] address, multiplexer_1_out, PCout;
  wire [15:0] ACCout, ALUout, multiplexer_2_out, multiplexer_3_out, RAMout;

  Multiplexer #(.width(8), .enable("false")) multiplexer_1 (
    .in0(PCout), .in1(address), .out(multiplexer_1_out), .sel(phase_1));
  Multiplexer #(.width(16), .enable("false")) multiplexer_2 (
    .in0(ACCout), .in1(in_1), .out(multiplexer_2_out), .sel(select_ram));
  Multiplexer #(.width(16), .enable("false")) multiplexer_3 (
    .in0(RAMout), .in1(ALUout), .out(multiplexer_3_out), .sel(select_acc));
  nor nor_1 (run, arthm_error, Control_end);
  and and_1 (and_1_out, print, phase_1);
  not not_1 (not_1_out, clock_1_out);
  Clock clock_1 (.out(clock_1_out));
  Clock clock_2 (.out(clock_2_out));
  Program_Counter PC (.Address(address), .select(select_pc), .overwrite(phase_1), .out_4(PCout));
  Flags u_Flags (.in_1(ACCout), .GT(flags));
  Register_part #(.width(16)) ACC (.D(multiplexer_3_out), .en(store_acc), .Q(ACCout), .clk(clock_3_out));  // open: clr
  Clock clock_3 (.out(clock_3_out));
  Register_part #(.width(16)) IR (.D(RAMout), .en(phase_0), .Q(out_2), .clk(clock_4_out));  // open: clr
  Clock clock_4 (.out(clock_4_out));
  ALU_main u_ALU (
    .A(ACCout), .B(RAMout), .S(op), .Enable(alu), .R(ALUout), .Overflow(ALU_overflow),
    .Division_by_zero(ALU_division_by_zero));
  Register_part #(.width(16)) register_1 (.D(RAMout), .en(and_1_out), .Q(out_3), .clk(clock_5_out));  // open: clr
  Clock clock_5 (.out(clock_5_out));
  Counter #(.width(1), .max('h1)) counter_1 (.Q(phase_1), .clk(not_1_out));  // open: load, D, count, carry, clr
  not not_2 (phase_0, phase_1);
  RAM #(.dataWidth(16), .bus("separate")) ram_1 (
    .addr(multiplexer_1_out), .din(multiplexer_2_out), .data(RAMout), .str(store_ram), .sel(run),
    .clk(clock_2_out), .ld(load_ram));  // open: clr
  Control Control (
    .\input (out_2), .flags(flags), .address(address), .store_acc(Control_store_acc),
    .load_ram(Control_load_ram), .store_ram(Control_store_ram), .select_ram(select_ram), .\end (Control_end),
    .op(op), .select_acc(select_acc), .activate_alu(alu), .print(print), .select_pc(select_pc));
  and and_2 (store_ram, phase_1, Control_store_ram);
  or or_1 (arthm_error, ALU_overflow, ALU_division_by_zero);
  or or_2 (load_ram, Control_load_ram, phase_0);
  and and_3 (store_acc, Control_store_acc, phase_1);

  // Other names for the same wires on the sheet: in[15:0] = in_1; IRout[15:0] = out_2

  // Notes on the sheet:
  //   Phase Counter
endmodule

module Register (
  input  [7:0] in,
  input  load,
  output [7:0] out
);

  D_Flip_Flop d_ff_1 (.clk(load), .D(in[0]), .Q(out[0]));  // open: Qn, preset, en, reset
  D_Flip_Flop d_ff_2 (.clk(load), .D(in[1]), .Q(out[1]));  // open: Qn, preset, en, reset
  D_Flip_Flop d_ff_3 (.clk(load), .D(in[2]), .Q(out[2]));  // open: Qn, preset, en, reset
  D_Flip_Flop d_ff_4 (.clk(load), .D(in[3]), .Q(out[3]));  // open: Qn, preset, en, reset
  D_Flip_Flop d_ff_5 (.clk(load), .D(in[4]), .Q(out[4]));  // open: Qn, preset, en, reset
  D_Flip_Flop d_ff_6 (.clk(load), .D(in[5]), .Q(out[5]));  // open: Qn, preset, en, reset
  D_Flip_Flop d_ff_7 (.clk(load), .D(in[6]), .Q(out[6]));  // open: Qn, preset, en, reset
  D_Flip_Flop d_ff_8 (.clk(load), .D(in[7]), .Q(out[7]));  // open: Qn, preset, en, reset
endmodule

module Control (
  input  [15:0] \input ,
  input  [5:0] flags,
  output [7:0] address,
  output store_acc,
  output load_ram,
  output store_ram,
  output select_ram,
  output \end ,
  output [2:0] op,
  output select_acc,
  output activate_alu,
  output print,
  output select_pc
);

  wire and_2_out, and_3_out, and_4_out, and_5_out, and_8_out, and_9_out, and_10_out, and_11_out, and_12_out,
       and_13_out, and_14_out, and_15_out, not_1_out, not_2_out, not_3_out, not_4_out, not_5_out, not_6_out,
       not_7_out, not_8_out, not_9_out, not_10_out, not_11_out, not_12_out, not_13_out, not_14_out,
       not_15_out, not_16_out, not_17_out, not_19_out, not_20_out, not_21_out, not_22_out, not_23_out,
       or_2_out;

  not not_1 (not_1_out, \input [10]);
  not not_2 (not_2_out, \input [13]);
  and and_1 (store_ram, \input [10], \input [11]);
  not not_3 (not_3_out, \input [8]);
  not not_4 (not_4_out, \input [11]);
  not not_5 (not_5_out, \input [10]);
  not not_6 (not_6_out, \input [11]);
  not not_7 (not_7_out, \input [9]);
  and and_2 (and_2_out, not_3_out, not_7_out, \input [10], not_6_out, flags[0]);
  and and_3 (and_3_out, \input [8], \input [9], not_5_out, not_4_out, 1'b1);
  and and_4 (and_4_out, \input [8], \input [9], not_1_out, \input [11]);
  and and_5 (and_5_out, \input [12], not_2_out);
  not not_8 (not_8_out, \input [8]);
  not not_9 (not_9_out, \input [9]);
  and and_6 (activate_alu, \input [12], not_10_out);
  not not_10 (not_10_out, \input [13]);
  not not_11 (not_11_out, \input [12]);
  and and_7 (print, not_11_out, \input [13]);
  not not_12 (not_12_out, \input [9]);
  not not_13 (not_13_out, \input [8]);
  not not_14 (not_14_out, \input [11]);
  and and_8 (and_8_out, \input [8], not_12_out, \input [10], not_14_out, flags[1]);
  or or_1 (store_acc, and_4_out, and_5_out);
  not not_15 (not_15_out, \input [12]);
  and and_9 (and_9_out, not_15_out, \input [13]);
  Multiplexer #(.select(4), .width(3)) multiplexer_1 (
    .in0(3'b000), .in1(3'b000), .in2(3'b000), .in3(3'b000), .in4(3'b000), .in5(3'b000), .in6(3'b001),
    .in7(3'b010), .in8(3'b011), .in9(3'b100), .in10(3'b000), .in11(3'b000), .in12(3'b000), .in13(3'b000),
    .in14(3'b000), .in15(3'b000), .out(op), .sel(\input [11:8]));  // open: en
  and and_10 (and_10_out, not_8_out, not_9_out, \input [10], \input [11]);
  not not_16 (not_16_out, \input [11]);
  not not_17 (not_17_out, \input [11]);
  and and_11 (and_11_out, not_13_out, \input [9], \input [10], not_16_out, flags[2]);
  and and_12 (and_12_out, \input [8], \input [9], \input [10], not_17_out, flags[3]);
  or or_2 (or_2_out, and_3_out, and_2_out, and_8_out, and_11_out, and_12_out, and_14_out, and_13_out);
  not not_18 (select_acc, and_10_out);
  not not_19 (not_19_out, \input [9]);
  not not_20 (not_20_out, \input [10]);
  not not_21 (not_21_out, \input [9]);
  not not_22 (not_22_out, \input [10]);
  not not_23 (not_23_out, \input [8]);
  and and_13 (and_13_out, \input [8], not_19_out, not_20_out, \input [11], flags[5]);
  and and_14 (and_14_out, not_23_out, not_21_out, not_22_out, \input [11], flags[4]);
  or or_3 (load_ram, store_acc, and_9_out);
  and and_15 (and_15_out, \input [12], \input [13], or_2_out);
  not not_24 (select_pc, and_15_out);

  assign address = \input [7:0];
  assign \end  = \input [14];
  assign select_ram = \input [12];
endmodule

module Program_Counter (
  input  [7:0] Address,
  input  select,
  input  overwrite,
  output [7:0] out_4
);

  wire [7:0] adder_1_out, multiplexer_1_out;

  Multiplexer #(.width(8), .enable("false")) multiplexer_1 (
    .in0(Address), .in1(adder_1_out), .out(multiplexer_1_out), .sel(select));
  Register register_1 (.in(multiplexer_1_out), .load(overwrite), .out(out_4));
  Adder adder_1 (.a(out_4), .b(8'h1), .out(adder_1_out));  // open: cin, cout
endmodule

module Flags (
  input  [15:0] in_1,
  output [5:0] GT
);

  wire not_1_out, not_2_out;

  or or_1 (GT[1], in_1[0], in_1[1], in_1[2], in_1[3], in_1[4], in_1[5], in_1[6], in_1[7], in_1[8], in_1[9], in_1[10], in_1[11], in_1[12], in_1[13], in_1[14], in_1[15]);
  not not_1 (not_1_out, GT[1]);
  not not_2 (not_2_out, in_1[15]);
  not not_3 (GT[3], GT[1]);
  not not_4 (GT[5], in_1[15]);
  or or_2 (GT[0], not_1_out, in_1[15]);
  and and_1 (GT[2], not_2_out, GT[1]);

  assign GT[4] = in_1[15];

  // Notes on the sheet:
  //   LE
  //   DZ
  //   EQ
  //   GE
  //   LT
endmodule
